// Logisim project project.circ as structural Verilog: 12 circuits, main circuit main
module main (
  input  in_1,
  output [15:0] out_2
);

  wire undriven;
  wire [2:0] registers_1_p3, registers_1_p5;
  wire [15:0] counter_1_q;

  Counter #(.width(16), .max('hffff)) counter_1 (.Q(counter_1_q), .clk(undriven));  // open: load, D, count, carry, clr
  ROM #(.addrWidth(16), .dataWidth(16)) rom_1 (.addr(counter_1_q), .data(out_2));  // open: sel
  Decoder #(.select(4)) decoder_1 (.sel(out_2[15:12]));  // open: out0, out1, out2, out3, out4, out5, out6, out7, out8, out9, out10, out11, out12, out13, out14, out15, en
  // registers registers_1: pin names not known; wires that end beside it: out_2[8:6], out_2[5:3], registers_1_p3, out_2[11:9], registers_1_p5
  my_ALU my_alu_1 ();  // open: in_1, in_2, in_3, out_4
  Adder #(.width(3)) adder_1 (.a(registers_1_p5), .b(registers_1_p3));  // open: out, cin, cout
  // AND_Gate and_1 is placed but not wired

  // Notes on the sheet:
  //   contents of rom_1 (hex, n*v repeats v):
  //   4000 4202 8440 8683
endmodule

module my_d_latch (
  input  in_1,
  input  in_2,
  output out_3
);

  wire and_1_out, and_2_out, nor_1_out, not_1_out;

  not not_1 (not_1_out, in_1);
  and and_1 (and_1_out, in_1, in_2);
  and and_2 (and_2_out, in_2, not_1_out);
  nor nor_1 (nor_1_out, and_1_out, out_3);
  nor nor_2 (out_3, nor_1_out, and_2_out);
endmodule

module my_d_flipflop (
  input  \input ,
  input  clk,
  output \output 
);

  wire d_latch_out_3, not_1_out;

  not not_1 (not_1_out, clk);
  my_d_latch d_latch (.in_1(\input ), .in_2(not_1_out), .out_3(d_latch_out_3));
  my_d_latch d_latch_2 (.in_1(d_latch_out_3), .in_2(clk), .out_3(\output ));
endmodule

module my_16bit_reg (
  input  [15:0] \input ,
  input  load,
  input  clk,
  output [15:0] \output 
);

  wire my_2_1_16bit_mux_1_output, my_2_1_16bit_mux_2_output, my_2_1_16bit_mux_3_output,
       my_2_1_16bit_mux_4_output, my_2_1_16bit_mux_5_output, my_2_1_16bit_mux_6_output,
       my_2_1_16bit_mux_7_output, my_2_1_16bit_mux_8_output, my_2_1_16bit_mux_9_output,
       my_2_1_16bit_mux_10_output, my_2_1_16bit_mux_11_output, my_2_1_16bit_mux_12_output,
       my_2_1_16bit_mux_13_output, my_2_1_16bit_mux_14_output, my_2_1_16bit_mux_15_output,
       my_2_1_16bit_mux_16_output, not_1_out;

  not not_1 (not_1_out, load);
  my_2_1_16bit_mux my_2_1_16bit_mux_1 (
    .input1(\input [1]), .input2(\output [1]), .selector(not_1_out), .\output (my_2_1_16bit_mux_1_output));
  my_2_1_16bit_mux my_2_1_16bit_mux_2 (
    .input1(\input [0]), .input2(\output [0]), .selector(not_1_out), .\output (my_2_1_16bit_mux_2_output));
  my_d_flipflop my_d_flipflop_1 (.\input (my_2_1_16bit_mux_2_output), .clk(clk), .\output (\output [0]));
  my_d_flipflop my_d_flipflop_2 (.\input (my_2_1_16bit_mux_1_output), .clk(clk), .\output (\output [1]));
  my_2_1_16bit_mux my_2_1_16bit_mux_3 (
    .input1(\input [2]), .input2(\output [2]), .selector(not_1_out), .\output (my_2_1_16bit_mux_3_output));
  my_d_flipflop my_d_flipflop_3 (.\input (my_2_1_16bit_mux_3_output), .clk(clk), .\output (\output [2]));
  my_2_1_16bit_mux my_2_1_16bit_mux_4 (
    .input1(\input [3]), .input2(\output [3]), .selector(not_1_out), .\output (my_2_1_16bit_mux_4_output));
  my_d_flipflop my_d_flipflop_4 (.\input (my_2_1_16bit_mux_4_output), .clk(clk), .\output (\output [3]));
  my_2_1_16bit_mux my_2_1_16bit_mux_5 (
    .input1(\input [4]), .input2(\output [4]), .selector(not_1_out), .\output (my_2_1_16bit_mux_5_output));
  my_d_flipflop my_d_flipflop_5 (.\input (my_2_1_16bit_mux_5_output), .clk(clk), .\output (\output [4]));
  my_2_1_16bit_mux my_2_1_16bit_mux_6 (
    .input1(\input [5]), .input2(\output [5]), .selector(not_1_out), .\output (my_2_1_16bit_mux_6_output));
  my_d_flipflop my_d_flipflop_6 (.\input (my_2_1_16bit_mux_6_output), .clk(clk), .\output (\output [5]));
  my_2_1_16bit_mux my_2_1_16bit_mux_7 (
    .input1(\input [6]), .input2(\output [6]), .selector(not_1_out), .\output (my_2_1_16bit_mux_7_output));
  my_d_flipflop my_d_flipflop_7 (.\input (my_2_1_16bit_mux_7_output), .clk(clk), .\output (\output [6]));
  my_2_1_16bit_mux my_2_1_16bit_mux_8 (
    .input1(\input [7]), .input2(\output [7]), .selector(not_1_out), .\output (my_2_1_16bit_mux_8_output));
  my_d_flipflop my_d_flipflop_8 (.\input (my_2_1_16bit_mux_8_output), .clk(clk), .\output (\output [7]));
  my_2_1_16bit_mux my_2_1_16bit_mux_9 (
    .input1(\input [8]), .input2(\output [8]), .selector(not_1_out), .\output (my_2_1_16bit_mux_9_output));
  my_d_flipflop my_d_flipflop_9 (.\input (my_2_1_16bit_mux_9_output), .clk(clk), .\output (\output [8]));
  my_2_1_16bit_mux my_2_1_16bit_mux_10 (
    .input1(\input [9]), .input2(\output [9]), .selector(not_1_out), .\output (my_2_1_16bit_mux_10_output));
  my_2_1_16bit_mux my_2_1_16bit_mux_11 (
    .input1(\input [10]), .input2(\output [10]), .selector(not_1_out), .\output (my_2_1_16bit_mux_11_output));
  my_d_flipflop my_d_flipflop_10 (.\input (my_2_1_16bit_mux_10_output), .clk(clk), .\output (\output [9]));
  my_d_flipflop my_d_flipflop_11 (.\input (my_2_1_16bit_mux_11_output), .clk(clk), .\output (\output [10]));
  my_2_1_16bit_mux my_2_1_16bit_mux_12 (
    .input1(\input [11]), .input2(\output [11]), .selector(not_1_out), .\output (my_2_1_16bit_mux_12_output));
  my_d_flipflop my_d_flipflop_12 (.\input (my_2_1_16bit_mux_12_output), .clk(clk), .\output (\output [11]));
  my_2_1_16bit_mux my_2_1_16bit_mux_13 (
    .input1(\input [12]), .input2(\output [12]), .selector(not_1_out), .\output (my_2_1_16bit_mux_13_output));
  my_d_flipflop my_d_flipflop_13 (.\input (my_2_1_16bit_mux_13_output), .clk(clk), .\output (\output [12]));
  my_2_1_16bit_mux my_2_1_16bit_mux_14 (
    .input1(\input [13]), .input2(\output [13]), .selector(not_1_out), .\output (my_2_1_16bit_mux_14_output));
  my_d_flipflop my_d_flipflop_14 (.\input (my_2_1_16bit_mux_14_output), .clk(clk), .\output (\output [13]));
  my_2_1_16bit_mux my_2_1_16bit_mux_15 (
    .input1(\input [14]), .input2(\output [14]), .selector(not_1_out), .\output (my_2_1_16bit_mux_15_output));
  my_d_flipflop my_d_flipflop_15 (.\input (my_2_1_16bit_mux_15_output), .clk(clk), .\output (\output [14]));
  my_2_1_16bit_mux my_2_1_16bit_mux_16 (
    .input1(\input [15]), .input2(\output [15]), .selector(not_1_out), .\output (my_2_1_16bit_mux_16_output));
  my_d_flipflop my_d_flipflop_16 (.\input (my_2_1_16bit_mux_16_output), .clk(clk), .\output (\output [15]));
endmodule

module my_3_8_decoder (
  input  in_1,
  input  in_2,
  input  in_3,
  input  load,
  output out_5,
  output out_6,
  output out_7,
  output out_8,
  output out_9,
  output out_10,
  output out_11,
  output out_12
);

  wire not_1_out, not_2_out, not_3_out, not_4_out, not_5_out, not_6_out, not_7_out, not_8_out, not_9_out,
       not_10_out, not_11_out, not_12_out;

  not not_1 (not_1_out, in_1);
  not not_2 (not_2_out, in_2);
  not not_3 (not_3_out, in_3);
  not not_4 (not_4_out, in_1);
  not not_5 (not_5_out, in_2);
  not not_6 (not_6_out, in_1);
  not not_7 (not_7_out, in_3);
  not not_8 (not_8_out, in_1);
  not not_9 (not_9_out, in_2);
  not not_10 (not_10_out, in_3);
  not not_11 (not_11_out, in_2);
  not not_12 (not_12_out, in_3);
  and and_1 (out_5, not_1_out, not_2_out, load, not_3_out);
  and and_2 (out_6, not_4_out, not_5_out, load, in_3);
  and and_3 (out_7, not_6_out, in_2, load, not_7_out);
  and and_4 (out_8, not_8_out, in_2, load, in_3);
  and and_5 (out_9, in_1, not_9_out, load, not_10_out);
  and and_6 (out_10, in_1, not_11_out, load, in_3);
  and and_7 (out_11, in_1, in_2, load, not_12_out);
  and and_8 (out_12, in_1, in_2, load, in_3);
endmodule

module my_2_1_16bit_mux (
  input  input1,
  input  input2,
  input  selector,
  output \output 
);

  wire and_1_out, and_2_out, not_1_out;

  not not_1 (not_1_out, selector);
  and and_1 (and_1_out, input1, not_1_out);
  and and_2 (and_2_out, input2, selector);
  or or_1 (\output , and_1_out, and_2_out);
endmodule

module registers (
  input  [15:0] \input ,
  input  [2:0] fetchNumber,
  input  [2:0] storeNumber,
  input  load,
  input  [2:0] fetchNumber_2,
  input  clk,
  output [15:0] \output ,
  output [15:0] output_2
);

  wire my_3_8_decoder_1_out_5, my_3_8_decoder_1_out_6, my_3_8_decoder_1_out_7, my_3_8_decoder_1_out_8,
       my_3_8_decoder_1_out_9, my_3_8_decoder_1_out_10, my_3_8_decoder_1_out_11, my_3_8_decoder_1_out_12;
  wire [15:0] my_16bit_reg_1_output, my_16bit_reg_2_output, my_16bit_reg_3_output, my_16bit_reg_4_output,
       R0_2_output, R0_3_output, R0_output, R3_output;

  my_3_8_decoder my_3_8_decoder_1 (
    .in_1(storeNumber[2]), .in_2(storeNumber[1]), .in_3(storeNumber[0]), .load(load),
    .out_5(my_3_8_decoder_1_out_5), .out_6(my_3_8_decoder_1_out_6), .out_7(my_3_8_decoder_1_out_7),
    .out_8(my_3_8_decoder_1_out_8), .out_9(my_3_8_decoder_1_out_9), .out_10(my_3_8_decoder_1_out_10),
    .out_11(my_3_8_decoder_1_out_11), .out_12(my_3_8_decoder_1_out_12));
  my_16bit_reg R0 (.load(my_3_8_decoder_1_out_5), .clk(clk), .\input (\input ), .\output (R0_output));
  my_16bit_reg R0_2 (.load(my_3_8_decoder_1_out_6), .clk(clk), .\input (\input ), .\output (R0_2_output));
  my_16bit_reg R0_3 (.load(my_3_8_decoder_1_out_7), .clk(clk), .\input (\input ), .\output (R0_3_output));
  my_16bit_reg R3 (.load(my_3_8_decoder_1_out_8), .clk(clk), .\input (\input ), .\output (R3_output));
  my_16bit_reg my_16bit_reg_1 (
    .load(my_3_8_decoder_1_out_9), .clk(clk), .\input (\input ), .\output (my_16bit_reg_1_output));
  my_16bit_reg my_16bit_reg_2 (
    .load(my_3_8_decoder_1_out_10), .clk(clk), .\input (\input ), .\output (my_16bit_reg_2_output));
  my_16bit_reg my_16bit_reg_3 (
    .load(my_3_8_decoder_1_out_11), .clk(clk), .\input (\input ), .\output (my_16bit_reg_3_output));
  my_16bit_reg my_16bit_reg_4 (
    .load(my_3_8_decoder_1_out_12), .clk(clk), .\input (\input ), .\output (my_16bit_reg_4_output));
  my_8_1_3bit_mux my_8_1_3bit_mux_1 (
    .in_1(R0_output), .in_2(R0_2_output), .in_3(R0_3_output), .in_4(R3_output), .in_5(my_16bit_reg_1_output),
    .in_6(my_16bit_reg_2_output), .in_7(my_16bit_reg_3_output), .in_8(my_16bit_reg_4_output),
    .in_9(fetchNumber[2]), .in_10(fetchNumber[1]), .in_11(fetchNumber[0]), .out_12(\output ));
  my_8_1_3bit_mux my_8_1_3bit_mux_2 (
    .in_1(R0_output), .in_2(R0_2_output), .in_3(R0_3_output), .in_4(R3_output), .in_5(my_16bit_reg_1_output),
    .in_6(my_16bit_reg_2_output), .in_7(my_16bit_reg_3_output), .in_8(my_16bit_reg_4_output),
    .in_9(fetchNumber_2[2]), .in_10(fetchNumber_2[1]), .in_11(fetchNumber_2[0]), .out_12(output_2));
endmodule

module my_2_4_decoder (
  input  in_1,
  input  in_2,
  input  in_3,
  output out_4,
  output out_5,
  output out_6,
  output out_7
);

  wire not_1_out, not_2_out, not_3_out, not_4_out;

  not not_1 (not_1_out, in_1);
  not not_2 (not_2_out, in_2);
  not not_3 (not_3_out, in_1);
  not not_4 (not_4_out, in_2);
  and and_1 (out_4, not_1_out, not_2_out, in_3);
  and and_2 (out_5, not_3_out, in_2, in_3);
  and and_3 (out_6, in_1, not_4_out, in_3);
  and and_4 (out_7, in_1, in_2, in_3);
endmodule

module my_8_1_3bit_mux (
  input  [15:0] in_1,
  input  [15:0] in_2,
  input  [15:0] in_3,
  input  [15:0] in_4,
  input  [15:0] in_5,
  input  [15:0] in_6,
  input  [15:0] in_7,
  input  [15:0] in_8,
  input  in_9,
  input  in_10,
  input  in_11,
  output [15:0] out_12
);

  wire [15:0] and_1_out, and_2_out, and_3_out, and_4_out, and_5_out, and_6_out, and_7_out, and_8_out,
       my_1_16_extender_1_out_2, my_1_16_extender_2_out_2, my_1_16_extender_3_out_2, not_1_out, not_2_out,
       not_3_out, not_4_out, not_5_out, not_6_out, not_7_out, not_8_out, not_9_out, not_10_out, not_11_out,
       not_12_out;

  my_1_16_extender my_1_16_extender_1 (.in_1(in_9), .out_2(my_1_16_extender_1_out_2));
  my_1_16_extender my_1_16_extender_2 (.in_1(in_10), .out_2(my_1_16_extender_2_out_2));
  assign not_1_out = ~my_1_16_extender_1_out_2;  // NOT_Gate not_1, 16 bits wide
  assign not_2_out = ~my_1_16_extender_2_out_2;  // NOT_Gate not_2, 16 bits wide
  assign not_3_out = ~my_1_16_extender_3_out_2;  // NOT_Gate not_3, 16 bits wide
  assign not_4_out = ~my_1_16_extender_1_out_2;  // NOT_Gate not_4, 16 bits wide
  assign not_5_out = ~my_1_16_extender_2_out_2;  // NOT_Gate not_5, 16 bits wide
  assign not_6_out = ~my_1_16_extender_1_out_2;  // NOT_Gate not_6, 16 bits wide
  assign not_7_out = ~my_1_16_extender_3_out_2;  // NOT_Gate not_7, 16 bits wide
  assign not_8_out = ~my_1_16_extender_1_out_2;  // NOT_Gate not_8, 16 bits wide
  assign not_9_out = ~my_1_16_extender_2_out_2;  // NOT_Gate not_9, 16 bits wide
  assign not_10_out = ~my_1_16_extender_3_out_2;  // NOT_Gate not_10, 16 bits wide
  assign not_11_out = ~my_1_16_extender_2_out_2;  // NOT_Gate not_11, 16 bits wide
  assign not_12_out = ~my_1_16_extender_3_out_2;  // NOT_Gate not_12, 16 bits wide
  my_1_16_extender my_1_16_extender_3 (.in_1(in_11), .out_2(my_1_16_extender_3_out_2));
  assign and_1_out = in_1 & not_1_out & not_2_out & not_3_out;  // AND_Gate and_1, 16 bits wide
  assign and_2_out = in_2 & not_4_out & not_5_out & my_1_16_extender_3_out_2;  // AND_Gate and_2, 16 bits wide
  assign and_3_out = in_3 & not_6_out & my_1_16_extender_2_out_2 & not_7_out;  // AND_Gate and_3, 16 bits wide
  assign and_4_out = in_4 & not_8_out & my_1_16_extender_2_out_2 & my_1_16_extender_3_out_2;  // AND_Gate and_4, 16 bits wide
  assign and_5_out = in_5 & my_1_16_extender_1_out_2 & not_9_out & not_10_out;  // AND_Gate and_5, 16 bits wide
  assign and_6_out = in_6 & my_1_16_extender_1_out_2 & not_11_out & my_1_16_extender_3_out_2;  // AND_Gate and_6, 16 bits wide
  assign and_7_out = in_7 & my_1_16_extender_1_out_2 & my_1_16_extender_2_out_2 & not_12_out;  // AND_Gate and_7, 16 bits wide
  assign and_8_out = in_8 & my_1_16_extender_1_out_2 & my_1_16_extender_2_out_2 & my_1_16_extender_3_out_2;  // AND_Gate and_8, 16 bits wide
  assign out_12 = and_1_out | and_2_out | and_3_out | and_4_out | and_5_out | and_6_out | and_7_out | and_8_out;  // OR_Gate or_1, 16 bits wide
endmodule

module my_1_3_extender (
  input  in_1,
  output [2:0] out_2
);


  assign out_2 = {3{in_1}};
endmodule

module my_ALU (
  input  [15:0] in_1,
  input  [15:0] in_2,
  input  [1:0] in_3,
  output [15:0] out_4
);

  wire [15:0] adder_1_out, and_1_out, or_1_out;

  assign and_1_out = in_1 & in_2;  // AND_Gate and_1, 16 bits wide
  Adder #(.width(16)) adder_1 (.a(in_1), .b(in_2), .out(adder_1_out));  // open: cin, cout
  assign or_1_out = in_1 | in_2;  // OR_Gate or_1, 16 bits wide
  Multiplexer #(.select(2), .width(16)) multiplexer_1 (
    .in0(and_1_out), .in1(adder_1_out), .in2(or_1_out), .out(out_4), .sel(in_3));  // open: in3, en
endmodule

module my_1_16_extender (
  input  in_1,
  output [15:0] out_2
);


  assign out_2 = {16{in_1}};
endmodule
